// Logisim project adder4.circ as structural Verilog: 1 circuit, main circuit implementation
module implementation (
  input  [3:0] Ain,
  input  [3:0] Bin,
  input  Cinin,
  output [3:0] Sum_Out,
  output Carry_Out,
  output CarryOut
);

  wire and_1_out, and_2_out, and_3_out, and_4_out, and_5_out, and_6_out, and_7_out, and_8_out, or_1_out,
       or_2_out, or_3_out, xor_2_out, xor_4_out, xor_6_out, xor_8_out;

  // Probe on Ain
  // Probe on Bin
  // Probe on Sum_Out
  // Probe on Carry_Out
  xor xor_1 (Sum_Out[0], Cinin, xor_2_out);
  // Probe on Sum_Out[0]
  and and_1 (and_1_out, Ain[0], Bin[0]);
  and and_2 (and_2_out, Cinin, xor_2_out);
  or or_1 (or_1_out, and_1_out, and_2_out);
  xor xor_2 (xor_2_out, Bin[0], Ain[0]);
  xor xor_3 (Sum_Out[1], or_1_out, xor_4_out);
  and and_3 (and_3_out, Ain[1], Bin[1]);
  xor xor_4 (xor_4_out, Bin[1], Ain[1]);
  and and_4 (and_4_out, or_1_out, xor_4_out);
  or or_2 (or_2_out, and_3_out, and_4_out);
  and and_5 (and_5_out, Ain[2], Bin[2]);
  xor xor_5 (Sum_Out[2], or_2_out, xor_6_out);
  xor xor_6 (xor_6_out, Bin[2], Ain[2]);
  and and_6 (and_6_out, or_2_out, xor_6_out);
  or or_3 (or_3_out, and_5_out, and_6_out);
  and and_7 (and_7_out, Ain[3], Bin[3]);
  xor xor_7 (Sum_Out[3], or_3_out, xor_8_out);
  and and_8 (and_8_out, or_3_out, xor_8_out);
  xor xor_8 (xor_8_out, Bin[3], Ain[3]);
  or or_4 (Carry_Out, and_8_out, and_7_out);

  assign CarryOut = Carry_Out;

  // Other names for the same wires on the sheet: A[3:0] = Ain; A0 = Ain[0]; A1 = Ain[1]; A2 = Ain[2]; A3 = Ain[3];
  //   B[3:0] = Bin; B0 = Bin[0]; B1 = Bin[1]; B2 = Bin[2]; B3 = Bin[3]; C3 = Carry_Out; Cin = Cinin; S0 = Sum_Out[0];
  //   Sum[3:0] = Sum_Out; S1 = Sum_Out[1]; S2 = Sum_Out[2]; S3 = Sum_Out[3]

  // Notes on the sheet:
  //   Gi
  //   Pi
endmodule
